# Fritzing sketch Stage0 (saved by Fritzing 0.9.2b)
breadboards: 1

parts:
  Part1 = Triple Axis Accelerometer Breakout - ADXL335
  Part2 = Arduino Uno (Rev3)

nets:
  N1: Part1.ZOUT, Part2.A2
  N2: Part1.YOUT, Part2.A1
  N3: Part1.XOUT, Part2.A0
  GND: Part1.GND, Part2.GND
  VCC: Part1.VCC, Part2.5V
