# Fritzing sketch Stage1 (saved by Fritzing 0.9.2b)
breadboards: 1

parts:
  Part1 = Triple Axis Accelerometer Breakout - ADXL335
  Part2 = Arduino Uno (Rev3)
  VCC1 = Battery block 9V
  Part4 = Bluetooth Mate Silver

nets:
  N1: Part1.ZOUT, Part2.A2
  N2: Part1.YOUT, Part2.A1
  N3: Part1.XOUT, Part2.A0
  GND: Part1.GND, Part2.GND, VCC1.-, Part4.GND
  VCC: Part1.VCC, Part2.5V, VCC1.+, Part4.VCC
  N4: Part2.D0/RX, Part4.TX_5V
  N5: Part2.D1/TX, Part4.RX_5V
