# Fritzing sketch Stage2 (saved by Fritzing 0.9.2b)
breadboards: 1

parts:
  LED1 = LED - 5mm [color="Red (633nm)" package="5 mm [THT]"]
  LED2 = LED - 5mm [color="Green (555nm)" package="5 mm [THT]"]
  R1 = Resistor [tolerance=±5% resistance=470 package="2512 [SMD]"]
  R2 = Resistor [tolerance=±5% resistance=470 package="2512 [SMD]"]
  Part1 = Triple Axis Accelerometer Breakout - ADXL335
  Part2 = Arduino Uno (Rev3)
  VCC1 = Battery block 9V
  R3 = Resistor [tolerance=±5% resistance=470 package="2512 [SMD]"]
  LED5 = smd LED [color="Green (555nm)" package="1206 [SMD]"]
  Part4 = Bluetooth Mate Silver

nets:
  N1: LED1.cathode, R1.Pin_0
  N2: LED1.anode, Part2.D13/SCK
  N3: LED2.cathode, R2.Pin_0
  N4: LED2.anode, Part2.D12/MISO
  GND: R1.Pin_1, R2.Pin_1, Part1.GND, Part2.GND, VCC1.-, R3.Pin_1, Part4.GND
  N5: Part1.ZOUT, Part2.A2
  N6: Part1.YOUT, Part2.A1
  N7: Part1.XOUT, Part2.A0
  VCC: Part1.VCC, Part2.5V, VCC1.+, Part4.VCC
  N8: Part2.D11_PWM/MOSI, LED5.anode
  N9: Part2.D0/RX, Part4.TX_5V
  N10: Part2.D1/TX, Part4.RX_5V
  N11: R3.Pin_0, LED5.cathode
